# Fritzing sketch arduino_ethernet_rfid (saved by Fritzing 0.9.2b)
breadboards: 1

parts:
  Part3 = RFID-RC522-v2
  R1 = Resistor [tolerance=±5% resistance=330 package="0805 [SMD]"]
  R2 = Resistor [tolerance=±5% resistance=330 package="0805 [SMD]"]
  LED1 = LED - 3mm [color="Red (633nm)" package="3 mm [THT]"]
  LED2 = LED - 3mm [color="Green (560nm)" package="3 mm [THT]"]
  KEYPAD1 = Membrane Matrix Keypad
  R4 = Resistor [tolerance=±5% resistance=330 package="0805 [SMD]"]
  R5 = Resistor [tolerance=±5% resistance=330 package="0805 [SMD]"]
  R6 = Resistor [tolerance=±5% resistance=330 package="0805 [SMD]"]
  Part1 = Arduino Uno (Rev3)
  R7 = Resistor [tolerance=±5% resistance=330 package="0805 [SMD]"]
  R8 = Resistor [tolerance=±5% resistance=330 package="0805 [SMD]"]
  Part4 = Arduino Ethernet Shield (Rev3)  # not connected
  R9 = Resistor [tolerance=±5% resistance=330 package="0805 [SMD]"]

nets:
  N1: Part3.SDA, Part1.D9_PWM
  N2: Part3.SCK, Part1.D13/SCK
  N3: Part3.MOSI, Part1.D11_PWM/MOSI
  N4: Part3.MISO, Part1.D12/MISO
  GND: Part3.GND, LED1.cathode, LED2.cathode, R6.Pin_1, Part1.GND
  N5: Part3.RST, Part1.D8
  N6: Part3.3_3V, Part1.3V3
  N7: R1.Pin_0, LED2.anode
  N8: R1.Pin_1, Part1.D4
  N9: R2.Pin_0, LED1.anode
  N10: R2.Pin_1, Part1.D3_PWM
  N11: KEYPAD1.1, R4.Pin_0, Part1.5V
  N12: KEYPAD1.2, R4.Pin_1, R5.Pin_0
  N13: KEYPAD1.3, R5.Pin_1, R9.Pin_0
  N14: KEYPAD1.4, R9.Pin_1
  N15: KEYPAD1.5, R6.Pin_0, Part1.A0, R7.Pin_0
  N16: KEYPAD1.6, R7.Pin_1, R8.Pin_0
  N17: KEYPAD1.7, R8.Pin_1

custom parts:
  RFID-RC522-v2: A simple China made RFID-RC522 Reader; do check the pin labels, as this is a MFRC522 based clone.
  Membrane Matrix Keypad: Membrane Matrix 3x4 Keypad
